# Fritzing sketch tracker (saved by Fritzing 0.9.3b)
circuit board: 7.41082cm x 4.247cm
breadboards: 1

parts:
  ESP8266 = ESP8266 WiFi Module [part_number=ESP8266]
  Arduino_PRO = Arduino Pro Mini v13
  GY-NEO6MV3 = SUP500F [package=sup500f]
  MicroSD = SparkFun - microSD Transflash

nets:
  N1: ESP8266.RXD, Arduino_PRO.D3_PWM
  VCC: ESP8266.VCC, ESP8266.CH_PD, Arduino_PRO.VCC, GY-NEO6MV3.VCC, MicroSD.VCC
  GND: ESP8266.GND, Arduino_PRO.GND, GY-NEO6MV3.GND, MicroSD.GND
  N2: ESP8266.TXD, Arduino_PRO.D2
  N3: Arduino_PRO.D11_PWM/MOSI, GY-NEO6MV3.TX-O
  N4: Arduino_PRO.D10_PWM/SS, GY-NEO6MV3.RX-I

custom parts:
  ESP8266 WiFi Module: Generic WiFi Module based on the ESP8266 with onboard PCB antenna and UART communications
